# Fritzing sketch DispensingMechanism (saved by Fritzing 0.9.3b)
breadboards: 1

parts:
  U1 = NodeMCU v3.0
  M1 = Dagu DGServo 9g (Top view) [part_number=RS001B]
  M2 = Dagu DGServo 9g (Top view) [part_number=RS001B]
  M3 = Dagu DGServo 9g (Top view) [part_number=RS001B]
  S1 = Pushbutton [package="[THT]"]
  S2 = Pushbutton [package="[THT]"]
  S3 = Pushbutton [package="[THT]"]

nets:
  N1: U1.D1, M3.pulse
  N2: U1.D2, M2.pulse
  N3: U1.D3, M1.pulse
  N4: U1.D4, S2.Pin_3, S2.Pin_4
  N5: U1.D5, S1.Pin_3, S1.Pin_4
  N6: U1.D6, S3.Pin_3, S3.Pin_4
  VCC: U1.VU, M1.vcc, M2.vcc, M3.vcc
  GND: U1.GND, M1.gnd, M2.gnd, M3.gnd, S1.Pin_1, S1.Pin_2, S2.Pin_1, S2.Pin_2, S3.Pin_1, S3.Pin_2

custom parts:
  NodeMCU v3.0: NodeMCU v3 Lua WIFI Development Board
