# Fritzing sketch homesecurity system (saved by Fritzing 0.9.3b)
breadboards: 1

parts:
  HC-SR04_Sensor_1 = HC-SR04 Ultrasonic Distance Sensor
  J1 = Piezo Speaker
  LED1 = smd LED [color="Red (633nm)" package="0603 [SMD]"]
  U1 = NodeMCU V1.0

nets:
  VCC: HC-SR04_Sensor_1.VCC, U1.Vin
  N1: HC-SR04_Sensor_1.TRIG, U1.D2
  N2: HC-SR04_Sensor_1.ECHO, U1.D1
  GND: HC-SR04_Sensor_1.GND, J1.pin1, LED1.cathode, U1.GND
  N3: J1.pin2, U1.D6
  N4: LED1.anode, U1.D7

custom parts:
  NodeMCU V1.0: ESP8266 based NodeMCU
