# Fritzing sketch lazertag (saved by Fritzing 0.9.3b)
breadboards: 1

parts:
  R1 = Photocell (LDR) [package=THT]
  Part1 = Arduino Uno (Rev3) - ICSP
  U1 = ESP8266 ESP-01 Upgraded WiFi Module [part_number=ESP8266]
  7_Segment1 = 7 Segment Display
  R2 = Resistor [tolerance=±5% resistance=220 package="2010 [SMD]"]
  R3 = Resistor [tolerance=±5% resistance=220 package="2010 [SMD]"]
  R4 = Resistor [tolerance=±5% resistance=220 package="2010 [SMD]"]
  R6 = Photocell (LDR) [package=THT]
  R5 = Photocell (LDR) [package=THT]
  R7 = Resistor [tolerance=±5% resistance=220 package="2010 [SMD]"]
  R8 = Resistor [tolerance=±5% resistance=220 package="2010 [SMD]"]
  VCC1 = Battery block 9V
  R9 = Photocell (LDR) [package=THT]
  R10 = Resistor [tolerance=±5% resistance=220 package="2010 [SMD]"]
  LED1 = LED - 5mm [color="Red (633nm)" package="5 mm [THT]"]
  LED2 = LED - 5mm [color="Red (633nm)" package="5 mm [THT]"]
  LED3 = LED - 5mm [color="Red (633nm)" package="5 mm [THT]"]
  LED4 = LED - 5mm [color="Red (633nm)" package="5 mm [THT]"]

nets:
  N1: R1.pin_0, Part1.5V, R2.Pin_1, R3.Pin_0, R6.pin_0, R5.pin_0, R9.pin_0
  N2: R1.pin_1, Part1.A0, R8.Pin_1
  N3: Part1.A1, R5.pin_1, R7.Pin_1
  N4: Part1.A2, R4.Pin_1, R6.pin_1
  N5: Part1.A3, R9.pin_1, R10.Pin_1
  N6: Part1.A4/SDA, LED4.anode
  N7: Part1.D8, LED1.anode
  N8: Part1.D9_PWM, 7_Segment1.Segment_A
  N9: Part1.D10_PWM/SS, LED2.anode
  N10: Part1.D11_PWM/MOSI, LED3.anode
  N11: Part1.D12/MISO, U1.RXD
  N12: Part1.D13/SCK, U1.TXD
  GND: Part1.GND, U1.GND, R4.Pin_0, R7.Pin_0, R8.Pin_0, VCC1.-, R10.Pin_0, LED1.cathode, LED2.cathode, LED3.cathode, LED4.cathode
  N13: Part1.D2, 7_Segment1.Segment_B
  N14: Part1.D3_PWM, 7_Segment1.Segment_C
  N15: Part1.D4, 7_Segment1.Segment_D
  N16: Part1.D5_PWM, 7_Segment1.Segment_E
  N17: Part1.D6_PWM, 7_Segment1.Segment_F
  N18: Part1.D7, 7_Segment1.Segment_G
  N19: Part1.3V3, U1.CH_PD
  N20: Part1.VIN, VCC1.+
  N21: 7_Segment1.common_cathode, R2.Pin_0, R3.Pin_1

custom parts:
  ESP8266 ESP-01 Upgraded WiFi Module: Upgraded Version ESP-01,all Flash are upgraded to 1M byte.Also support Cloud service remote transmission.

// code stored in the sketch: lazertag.ino
#include <SoftwareSerial.h>

SoftwareSerial espSerial(12, 13); // RX, TX

int LDR1 = A0; //for ldr sensors
int LDR2 = A1;
int LDR3 = A2;
int count = 0;


int A = 9; //for 7segment display
int B = 2;
int C = 3;
int D = 4;
int E = 5;
int F = 6;
int G = 7;
int P = 8;

void setup() {
  Serial.begin(9600);
  espSerial.begin(115200);

pinMode(LDR1, INPUT);  //LDR Pins
pinMode(LDR2, INPUT);
pinMode(LDR3, INPUT);

for(int pin = 2;pin<10;pin++){ // 7Segment display pins
  pinMode(pin,OUTPUT);
}

  // Connect to Wi-Fi network
  sendCommand("AT+CWJAP=\"your_ssid\",\"your_password\"");

  // Start server
  sendCommand("AT+CIPMUX=1");
  sendCommand("AT+CIPSERVER=1,80");
}

void zero(void){ //functions to print score on 7segment display
  digitalWrite(G, HIGH);
  digitalWrite(B, LOW);
  digitalWrite(C, LOW);
  digitalWrite(D, LOW);
  digitalWrite(E, LOW);
  digitalWrite(F, LOW);
  digitalWrite(A, LOW);
  digitalWrite(P, LOW);
}


void one(void){
 digitalWrite(A, HIGH);
 digitalWrite(B, LOW);
 digitalWrite(C, LOW);
 digitalWrite(D, HIGH);
 digitalWrite(E, HIGH);
 digitalWrite(F, HIGH);
 digitalWrite(G, HIGH);
  digitalWrite(P, LOW);
}
void two(void){
 digitalWrite(A, LOW);
 digitalWrite(B, LOW);
 digitalWrite(C, HIGH);
 digitalWrite(D, LOW);
 digitalWrite(E, LOW);
 digitalWrite(F, HIGH);
 digitalWrite(G, LOW);
  digitalWrite(P, LOW);
}
void three(void){
  digitalWrite(A, LOW);
  digitalWrite(B, LOW);
  digitalWrite(C, LOW);
  digitalWrite(D, LOW);
  digitalWrite(E, HIGH);
  digitalWrite(F, HIGH);
  digitalWrite(G, LOW);
  digitalWrite(P, LOW);
}

void four(void){
 digitalWrite(A, HIGH);
 digitalWrite(B, LOW);
 digitalWrite(C, LOW);
 digitalWrite(D, HIGH);
 digitalWrite(E, HIGH);
 digitalWrite(F, LOW);
 digitalWrite(G, LOW);
  digitalWrite(P, LOW);
}
void five(void){
 digitalWrite(A, LOW);
 digitalWrite(B, HIGH);
 digitalWrite(C, LOW);
 digitalWrite(D, LOW);
 digitalWrite(E, HIGH);
 digitalWrite(F, LOW);
 digitalWrite(G, LOW);
  digitalWrite(P, LOW);
}
void six(void){
 digitalWrite(A, LOW);
 digitalWrite(B, HIGH);
 digitalWrite(C, LOW);
 digitalWrite(D, LOW);
 digitalWrite(E, LOW);
 digitalWrite(F, LOW);
 digitalWrite(G, LOW);
  digitalWrite(P, LOW);
}
void seven(void){
  digitalWrite(A, LOW);
  digitalWrite(B, LOW);
  digitalWrite(C, LOW);
 digitalWrite(D, HIGH);
 digitalWrite(E, HIGH);
 digitalWrite(F, HIGH);
 digitalWrite(G, HIGH);
  digitalWrite(P, LOW);
}


void eight(void){
   digitalWrite(A, LOW);
   digitalWrite(B, LOW);
   digitalWrite(C, LOW);
   digitalWrite(D, LOW);
   digitalWrite(E, LOW);
   digitalWrite(F, LOW);
  digitalWrite(G, LOW);
  digitalWrite(P, LOW);
}
void nine(void){
 digitalWrite(A, LOW);
 digitalWrite(B, LOW);
 digitalWrite(C, LOW);
 digitalWrite(D, LOW);
 digitalWrite(E, HIGH);
 digitalWrite(F, LOW);
 digitalWrite(G, LOW);
  digitalWrite(P, LOW);
}



void loop() {
  int ldr1Value = analogRead(LDR1);
  int ldr2Value = analogRead(LDR2);
  int ldr3Value = analogRead(LDR3);
  
  // Check if any of the LDR sensors detects light
  if (ldr1Value > 500 || ldr2Value > 500 || ldr3Value > 500) {  //change the intensity '500' accordingly
    count++;
    Serial.println("Count: " + String(count));
  }
if (count == 0){ //Printing on 7 segment display
    zero();
    delay(1000);
  }
  if (count == 1){
    one();
    delay(1000);
  }
  if (count == 2){
    two();
    delay(1000);
  }
  if (count == 3){
    three();
    delay(1000);
  }
  if (count == 4){
    four();
    delay(1000);
  }
    if (count == 5){
    five();
    delay(1000);
  }
  
  
  // Listen for incoming client connections
  if (espSerial.available()) {
    String message = espSerial.readStringUntil('\n');
    Serial.println(message);
    if (message.indexOf("GET / ") != -1) {
      // Send HTML page with count value embedded
      sendResponse("<html><head><title>LDR Count</title></head><body><h1>LDR Count: " + String(count) + "</h1></body></html>");
    }
  }
}

void sendCommand(String command) {
  espSerial.println(command);
  delay(1000);
  while (espSerial.available()) {
    String response = espSerial.readStringUntil('\n');
    Serial.println(response);
  }
}

void sendResponse(String message) {
  String response = "HTTP/1.1 200 OK\r\nContent-Type: text/html\r\n\r\n";
  response += message;
  response += "\r\n";
  espSerial.print("AT+CIPSEND=0,");
  espSerial.println(response.length());
  delay(1000);
  espSerial.print(response);
  delay(1000);
}
