# Fritzing sketch roadbot (saved by Fritzing 0.9.3b)
breadboards: 1

parts:
  S1 = H-Bridge with L298N
  Part1 = Arduino Uno (Rev3) - ICSP
  M1 = fc-51 [package=THT]
  VCC2 = Battery
  M2 = DC Motor
  J1 = Basic Servo
  Part2 = Bluetooth HC-05 Macho
  M3 = fc-51 [package=THT]
  M4 = fc-51 [package=THT]
  M5 = fc-51 [package=THT]
  M6 = fc-51 [package=THT]
  M7 = DC Motor
  M8 = DC Motor
  M9 = DC Motor
  J2 = Basic Servo

nets:
  N1: S1.12V, VCC2.+
  N2: S1.GND, VCC2.-
  N3: S1.IN1, Part1.D13/SCK
  N4: S1.IN2, Part1.ICSP_MISO, Part1.D12/MISO
  N5: S1.IN3, Part1.D11_PWM/MOSI
  N6: S1.IN4, Part1.D10_PWM/SS
  N7: S1.M1-01, M2.pin_2, M9.pin_2
  N8: S1.M1-02, M2.pin_1, M9.pin_1
  N9: S1.M2-01, M7.pin_2, M8.pin_2
  N10: S1.M2-02, M7.pin_1, M8.pin_1
  N11: Part1.D8, J2.pulse
  N12: Part1.D9_PWM, J1.pulse
  N13: Part1.D0/RX, Part2.RXD
  N14: Part1.D1/TX, Part2.TXD
  N15: Part1.D2, M6.pin1
  N16: Part1.D3_PWM, M5.pin1
  N17: Part1.D4, M4.pin1
  N18: Part1.D5_PWM, M3.pin1
  N19: Part1.D6_PWM, M1.pin1
  VCC: Part1.5V, M1.pin3, J1.vcc, Part2.VCC, M3.pin3, M4.pin3, M5.pin3, M6.pin3, J2.vcc
  GND: Part1.GND, M1.pin2, J1.gnd, Part2.GND, M3.pin2, M4.pin2, M5.pin2, M6.pin2, J2.gnd

custom parts:
  H-Bridge with L298N: h-bridge
