# Fritzing sketch roadbot1 (saved by Fritzing 0.9.3b)
breadboards: 1

parts:
  Part6 = Arduino Mega 2560 (Rev3)
  S1 = H-Bridge with L298N
  J1 = Basic Servo
  J2 = Basic Servo
  HC-SR04_Sensor_1 = HC-SR04 Ultrasonic Distance Sensor
  Part7 = Bluetooth HC-05 Macho
  M1 = DC Motor
  HC-SR04_Sensor_2 = HC-SR04 Ultrasonic Distance Sensor
  HC-SR04_Sensor_3 = HC-SR04 Ultrasonic Distance Sensor
  HC-SR04_Sensor_4 = HC-SR04 Ultrasonic Distance Sensor
  HC-SR04_Sensor_5 = HC-SR04 Ultrasonic Distance Sensor
  M2 = DC Motor
  M3 = DC Motor
  M4 = DC Motor
  VCC1 = Battery

nets:
  N1: Part6.D13_PWM, S1.IN1
  N2: Part6.D12_PWM, S1.IN2
  N3: Part6.D11_PWM, S1.IN3
  N4: Part6.D10_PWM, S1.IN4
  VCC: Part6.5V, HC-SR04_Sensor_1.VCC, Part7.VCC, HC-SR04_Sensor_2.VCC, HC-SR04_Sensor_3.VCC, HC-SR04_Sensor_4.VCC, HC-SR04_Sensor_5.VCC
  GND: Part6.GND, HC-SR04_Sensor_1.GND, Part7.GND, HC-SR04_Sensor_2.GND, HC-SR04_Sensor_3.GND, HC-SR04_Sensor_4.GND, HC-SR04_Sensor_5.GND
  N5: Part6.D0_RX0, Part7.TXD
  N6: Part6.D1_TX0, Part7.RXD
  N7: Part6.D6_PWM, J1.pulse
  N8: Part6.D7_PWM, J2.pulse
  N9: Part6.D22, HC-SR04_Sensor_5.TRIG
  N10: Part6.D23, HC-SR04_Sensor_5.ECHO
  N11: Part6.D26, HC-SR04_Sensor_1.TRIG
  N12: Part6.D27, HC-SR04_Sensor_1.ECHO
  N13: Part6.D30, HC-SR04_Sensor_2.TRIG
  N14: Part6.D31, HC-SR04_Sensor_2.ECHO
  N15: Part6.D34, HC-SR04_Sensor_3.TRIG
  N16: Part6.D35, HC-SR04_Sensor_3.ECHO
  N17: Part6.D38, HC-SR04_Sensor_4.TRIG
  N18: Part6.D39, HC-SR04_Sensor_4.ECHO
  12V: S1.12V, S1.5V, VCC1.+
  N19: S1.GND, VCC1.-
  N20: S1.M1-01, M1.pin_2, M2.pin_2
  N21: S1.M1-02, M1.pin_1, M2.pin_1
  N22: S1.M2-01, M3.pin_2, M4.pin_2
  N23: S1.M2-02, M3.pin_1, M4.pin_1
  GND_2: J1.gnd, J2.gnd
  VCC_2: J1.vcc, J2.vcc

custom parts:
  H-Bridge with L298N: h-bridge
