# Fritzing sketch smartbin (saved by Fritzing 0.9.3b)

parts:
  Part1 = Arduino Uno (Rev3)
  SM1 = 28BYJ-48 Stepper Motor [part_number=28BYJ-48]
  Driver1 = 28BYJ-48 Driver Module [part_number=ULN2003 package=THT]
  HC-SR04_Sensor_1 = HC-SR04 Ultrasonic Distance Sensor
  HC-SR04_Sensor_2 = HC-SR04 Ultrasonic Distance Sensor
  ESP32_Cam1 = ESP32 - CAM
  FTDI_Module1 = Adafruit FTDI Friend [part_number="Adafruit #284"]
  Prog_Switch1 = SWITCH_SPDT [package=kps-1290]
  HX711 = HX711 Weighing Sensor Module
  Load_Cell1 = Load Cell - Red/white/black/green
  VCC1 = Battery block 9V

nets:
  N1: Part1.D8, Driver1.IN2
  N2: Part1.D9_PWM, Driver1.IN1
  N3: Part1.D10_PWM/SS, HC-SR04_Sensor_1.ECHO
  N4: Part1.D11_PWM/MOSI, HC-SR04_Sensor_1.TRIG
  N5: Part1.D12/MISO, HC-SR04_Sensor_2.ECHO
  N6: Part1.D13/SCK, HC-SR04_Sensor_2.TRIG
  N7: Part1.D6_PWM, Driver1.IN4
  N8: Part1.D7, Driver1.IN3
  N9: SM1.blue-pin, Driver1.blue-pin
  N10: SM1.pink-pin, Driver1.pink-pin
  N11: SM1.yellow-pin, Driver1.yellow-pin
  N12: SM1.orange-pin, Driver1.orange-pin
  N13: SM1.red-pin, Driver1.red-pin
  N14: Driver1.GND, VCC1.-
  N15: Driver1.Vmotor, VCC1.+
  N16: ESP32_Cam1.GPIO13, HX711.CK/TX
  N17: ESP32_Cam1.GPIO12, HX711.DO/RX
  N18: ESP32_Cam1.GND#7, FTDI_Module1.GND
  5V: ESP32_Cam1.5V, FTDI_Module1.VCC
  N19: ESP32_Cam1.GPIO0, Prog_Switch1.O
  N20: ESP32_Cam1.GND#12, Prog_Switch1.P
  N21: ESP32_Cam1.GPIO3_/_RX, FTDI_Module1.TX
  N22: ESP32_Cam1.GPIO1_/_TX, FTDI_Module1.RX
  N23: HX711.E+, Load_Cell1.wire1
  N24: HX711.E-, Load_Cell1.wire3
  N25: HX711.A+, Load_Cell1.wire2
  N26: HX711.A-, Load_Cell1.wire4

notes:
  Both the arduino and the esp32 cam will be powered by one power bank.
  load cell, hx711 and esp32 cam will be powered by ftdi module, which recieves power from power bank
  Ultrasonic Sensors will be powered by arduino, stepper motor will be powered by 9v external battery to avoid load on arduino

custom parts:
  28BYJ-48 Stepper Motor: Unipolar Stepper Motor 28BYJ-48 Top coil - pink & orange Bottom coil - blue & yellow Common rail - red Connector pins: blue - pink - yellow - orange - red
  28BYJ-48 Driver Module: ULN2003 Driver Module for the 28BYJ-48 Unipolar Stepper Motor LED A - Blue wire - Bottom coil left LED B - Pink wire - Top coil left LED C - Yellow wire - Bottom coil right LED D - Orange wire - Top coil right Common rail - red Connector pins: blue - pink - yellow - orange - red Control pins - IN1 to IN4 Power pins - GND & Vmotor (5-12V) On/Off jumper (if removed, power to motor is cut).
  ESP32 - CAM: The ESP32-CAM has a very competitive small-size camera module that can operate independently as a minimum system with a footprint of only 27*40.5*4.5mm and a deep sleep current of up to 6mA.
  Adafruit FTDI Friend: Long gone are the days of parallel ports and serial ports. Now the USB port reigns supreme! But USB is hard, and you just want to transfer your every-day serial data from a microcontroller to computer. What now? Enter the FTDI Friend! The FTDI Friend is a tweaked out FTDI FT232RL chip adapter. Sure, like the well-known FTDI cable, it can provide power to your project and there are 4 signal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
  Load Cell - Red/white/black/green: A rectangle load cell/weighting pressure Sensor with four wires - Red, white, black, green. Normally corresponding with E+, E-, A+, A- respectively.
